// Logisim project Diagram.circ as structural Verilog: 1 circuit, main circuit main
module main (
  input  A,
  input  B,
  input  C,
  input  D,
  input  E,
  input  F,
  input  G
);

  wire and_1_out, and_2_out, and_3_out, and_4_out, and_5_out, and_6_out, and_7_out, and_8_out, and_9_out,
       and_10_out, and_11_out, and_12_out, and_13_out, and_14_out, not_1_out, not_2_out, not_3_out,
       not_4_out, not_5_out, not_6_out, not_7_out, or_1_out, or_2_out, or_3_out;

  not not_1 (not_1_out, A);
  not not_2 (not_2_out, B);
  not not_3 (not_3_out, C);
  not not_4 (not_4_out, D);
  not not_5 (not_5_out, E);
  not not_6 (not_6_out, F);
  not not_7 (not_7_out, G);
  and and_1 (and_1_out, not_3_out, not_1_out, not_4_out, not_4_out);
  and and_2 (and_2_out, not_1_out, E);
  and and_3 (and_3_out, not_1_out, D);
  and and_4 (and_4_out, not_1_out, F);
  and and_5 (and_5_out, not_1_out, C);
  and and_6 (and_6_out, not_1_out, not_3_out, E);
  or or_1 (or_1_out, and_2_out, and_3_out);
  and and_7 (and_7_out, F, not_1_out);
  and and_8 (and_8_out, A, not_3_out);
  and and_9 (and_9_out, not_7_out, not_1_out, not_4_out, not_5_out);
  or or_2 (or_2_out, G, and_6_out);
  and and_10 (and_10_out, C, A, not_5_out);
  and and_11 (and_11_out, not_1_out, not_3_out, not_5_out);
  or or_3 (or_3_out, and_7_out, and_5_out, and_8_out, and_9_out);
  and and_12 (and_12_out, A, C);
  and and_13 (and_13_out, A, not_3_out);
  LED ALUop1 (.in(and_1_out));
  LED ALUop2 (.in(or_1_out));
  LED RegDst2 (.in(and_11_out));
  LED RegWrite (.in(or_3_out));
  LED Branch (.in(and_14_out));
  and and_14 (and_14_out, not_1_out, D);
  LED Jump (.in(or_2_out));
  LED MemWrite (.in(and_12_out));
  LED MemRead (.in(and_13_out));
  LED StoreByte (.in(and_10_out));
  LED LoadByte (.in(not_5_out));
  LED JAL (.in(F));
  LED MemToReg (.in(A));
  LED RegDst1 (.in(and_4_out));
endmodule
